// Logisim project Circuits.circ as structural Verilog: 3 circuits, main circuit 2b
module _2b (
  input  x,
  input  y,
  output out_3
);

  wire nand_1_out, nand_2_out;

  nand nand_1 (nand_1_out, x, x);
  nand nand_2 (nand_2_out, y, y);
  nand nand_3 (out_3, nand_1_out, nand_2_out);
endmodule

module _4b (
  input  q,
  input  p,
  input  r,
  output s
);

  wire and_1_out, and_2_out, not_1_out, not_2_out;

  not not_1 (not_1_out, p);
  not not_2 (not_2_out, r);
  and and_1 (and_1_out, q, not_1_out);
  or or_1 (s, and_1_out, and_2_out);
  and and_2 (and_2_out, p, not_2_out);
endmodule

module _3e (
  input  in_1,
  input  in_2,
  output out_3
);

  wire not_1_out, or_1_out, xor_1_out;

  xor xor_1 (xor_1_out, in_1, in_2);
  not not_1 (not_1_out, in_2);
  or or_1 (or_1_out, in_1, not_1_out);
  nand nand_1 (out_3, xor_1_out, or_1_out);
endmodule
