// Logisim project Circuit.circ as structural Verilog: 1 circuit, main circuit main
module main (
  input  Input,
  output [2:0] Current_State
);

  wire clock_1_out, multiplexer_1_out, multiplexer_2_out, multiplexer_3_out, not_1_out;

  Clock clock_1 (.out(clock_1_out));
  D_Flip_Flop d_ff_1 (.clk(clock_1_out), .D(multiplexer_3_out), .Q(Current_State[0]));  // open: Qn, preset, en, reset
  D_Flip_Flop d_ff_2 (.clk(clock_1_out), .D(multiplexer_2_out), .Q(Current_State[1]));  // open: Qn, preset, en, reset
  D_Flip_Flop d_ff_3 (.clk(clock_1_out), .D(multiplexer_1_out), .Q(Current_State[2]));  // open: Qn, preset, en, reset
  Multiplexer #(.select(3), .disabled(0), .enable("false")) multiplexer_1 (
    .in0(1'b0), .in1(Input), .in2(Input), .in3(1'b1), .in4(1'b1), .in5(1'b0), .out(multiplexer_1_out),
    .sel(Current_State));  // open: in6, in7
  Multiplexer #(.select(3), .disabled(0), .enable("false")) multiplexer_2 (
    .in0(Input), .in1(not_1_out), .in2(not_1_out), .in3(1'b0), .in4(1'b0), .in5(Input),
    .out(multiplexer_2_out), .sel(Current_State));  // open: in6, in7
  not not_1 (not_1_out, Input);
  Multiplexer #(.select(3), .disabled(0), .enable("false")) multiplexer_3 (
    .in0(1'b1), .in1(Input), .in2(1'b1), .in3(1'b1), .in4(1'b1), .in5(1'b1), .out(multiplexer_3_out),
    .sel(Current_State));  // open: in6, in7
endmodule
